// Logisim project Final[1].circ as structural Verilog: 6 circuits, main circuit main
module main (
  input  in_1
);

  wire alu_1_out_5, and_1_out, clock_1_out, clock_2_out, clock_3_out, main_control_1_out_2,
       main_control_1_out_3, main_control_1_out_4, main_control_1_out_5, main_control_1_out_6,
       main_control_1_out_7, main_control_1_out_8, main_control_1_out_11, pull_resistor_1_node;
  wire [1:0] main_control_1_out_10;
  wire [3:0] alu_cntrl_1_out_3;
  wire [4:0] multiplexer_1_out;
  wire [5:0] ram_1_data_2;
  wire [25:0] ram_1_data;
  wire [27:0] adder_1_out;
  wire [31:0] adder_1_out_2, adder_2_out, alu_1_out_4, bit_extender_1_out, multiplexer_2_out,
       multiplexer_3_out, multiplexer_4_out, ram_2_data, register_1_q, registerfile_1_p1, registerfile_1_p7,
       registerfile_1_p8, shifter_2_out;

  Clock clock_1 (.out(clock_1_out));
  Register #(.width(32)) register_1 (
    .D(multiplexer_4_out), .Q(register_1_q), .clk(clock_1_out), .clr(in_1));  // open: en
  Adder #(.width(32)) adder_1 (
    .a(register_1_q), .b(32'h1), .out({adder_1_out_2[31:28], adder_1_out}));  // open: cin, cout
  Pull_Resistor #(.pull(1)) pull_resistor_1 (.node(pull_resistor_1_node));
  RAM #(.addrWidth(24), .dataWidth(32)) ram_1 (
    .addr(register_1_q[23:0]), .data({ram_1_data_2, ram_1_data}), .ld(pull_resistor_1_node));  // open: sel, clk, clr
  Main_Control main_control_1 (
    .in_1(ram_1_data_2), .out_2(main_control_1_out_2), .out_3(main_control_1_out_3),
    .out_4(main_control_1_out_4), .out_5(main_control_1_out_5), .out_6(main_control_1_out_6),
    .out_7(main_control_1_out_7), .out_8(main_control_1_out_8), .out_9(main_control_1_out_10[1]),
    .out_10(main_control_1_out_10[0]), .out_11(main_control_1_out_11));
  Multiplexer #(.width(5)) multiplexer_1 (
    .in0(ram_1_data[20:16]), .in1(ram_1_data[15:11]), .out(multiplexer_1_out), .sel(main_control_1_out_2));  // open: en
  Shifter #(.width(26)) shifter_1 (.in(ram_1_data), .\dist (5'b00010), .out(adder_1_out_2[25:0]));
  Clock clock_2 (.out(clock_2_out));
  assign bit_extender_1_out = {{16{ram_1_data[15]}}, ram_1_data[15:0]};  // Bit_Extender bit_extender_1
  // RegisterFile registerfile_1: pin names not known; wires that end beside it: registerfile_1_p1, clock_2_out, main_control_1_out_5, multiplexer_1_out, ram_1_data[25:21], ram_1_data[20:16], registerfile_1_p7, registerfile_1_p8, ram_1_data[5:0]
  Shifter #(.width(32)) shifter_2 (.in(bit_extender_1_out), .\dist (5'b00010), .out(shifter_2_out));
  Multiplexer #(.width(32), .enable("false")) multiplexer_2 (
    .in0(registerfile_1_p8), .in1(bit_extender_1_out), .out(multiplexer_2_out), .sel(main_control_1_out_3));
  ALU_CNTRL alu_cntrl_1 (.in_2(ram_1_data[5:0]), .in_1(main_control_1_out_10), .out_3(alu_cntrl_1_out_3));
  Adder #(.width(32)) adder_2 (
    .a({adder_1_out_2[31:28], adder_1_out}), .b(shifter_2_out), .out(adder_2_out));  // open: cin, cout
  ALU alu_1 (
    .out_4(alu_1_out_4), .out_5(alu_1_out_5), .in_1(multiplexer_2_out), .in_2(registerfile_1_p7),
    .in_3(alu_cntrl_1_out_3));
  and and_1 (and_1_out, main_control_1_out_8, alu_1_out_5);
  Multiplexer #(.width(32)) multiplexer_3 (
    .in0({adder_1_out_2[31:28], adder_1_out}), .in1(adder_2_out), .out(multiplexer_3_out), .sel(and_1_out));  // open: en
  Clock clock_3 (.out(clock_3_out));
  RAM #(.addrWidth(24), .dataWidth(32), .bus("separate")) ram_2 (
    .addr(alu_1_out_4[23:0]), .din(registerfile_1_p8), .data(ram_2_data), .str(main_control_1_out_7),
    .clk(clock_3_out), .ld(main_control_1_out_6));  // open: sel, clr
  Multiplexer #(.width(32)) multiplexer_4 (
    .in0(multiplexer_3_out), .in1({adder_1_out_2[31:28], 2'b00, adder_1_out_2[25:0]}),
    .out(multiplexer_4_out), .sel(main_control_1_out_11));  // open: en
  Multiplexer #(.width(32)) multiplexer_5 (
    .in0(alu_1_out_4), .in1(ram_2_data), .out(registerfile_1_p1), .sel(main_control_1_out_4));  // open: en

  // Notes on the sheet:
  //   PC + 4
  //   Instruction Memory
  //   Jump Address
  //   Register File
  //   Target Address
  //   Data Memory
  //   Write Data
endmodule

module ALU_CNTRL (
  input  [1:0] in_1,
  input  [5:0] in_2,
  output [3:0] out_3
);

  wire and_2_out, or_1_out;

  or or_1 (or_1_out, in_2[0], in_2[3]);
  and and_1 (out_3[3], ~in_1[0], in_1[0]);  // AND_Gate
  or or_2 (out_3[2], in_1[0], and_2_out);
  and and_2 (and_2_out, in_1[1], in_2[1]);
  or or_3 (out_3[1], ~in_2[2], ~in_1[1]);  // OR_Gate
  and and_3 (out_3[0], in_1[1], or_1_out);

  // Other names for the same wires on the sheet: ALUOp0 = in_1[0]; ALUOp1 = in_1[1]; f0 = in_2[0]; f1 = in_2[1];
  //   f2 = in_2[2]; f3 = in_2[3]; f4 = in_2[4]; op0 = out_3[0]; op1 = out_3[1]; op2 = out_3[2]; op3 = out_3[3]
endmodule

module Main_Control (
  input  [5:0] in_1,
  output out_2,
  output out_3,
  output out_4,
  output out_5,
  output out_6,
  output out_7,
  output out_8,
  output out_9,
  output out_10,
  output out_11
);

  and and_1 (out_2, ~in_1[5], ~in_1[4], ~in_1[3], ~in_1[2], ~in_1[1], ~in_1[0]);  // AND_Gate
  and and_2 (out_4, in_1[5], ~in_1[4], ~in_1[3], ~in_1[2], in_1[1], in_1[0]);  // AND_Gate
  and and_3 (out_7, in_1[5], ~in_1[4], in_1[3], ~in_1[2], in_1[1], in_1[0]);  // AND_Gate
  and and_4 (out_8, ~in_1[0], in_1[1], ~in_1[2], ~in_1[3], ~in_1[4], ~in_1[5]);  // AND_Gate
  and and_5 (out_11, ~in_1[0], in_1[1], ~in_1[2], ~in_1[3], ~in_1[4], ~in_1[5]);  // AND_Gate
  or or_1 (out_3, out_4, out_7);
  or or_2 (out_5, out_2, out_4);

  assign out_6 = out_4;
  assign out_9 = out_2;
  assign out_10 = out_8;

  // Other names for the same wires on the sheet: a0 = out_2; ALUOp1 = out_2; RegDst = out_2; a1 = out_4;
  //   MemRead = out_4; MemtoReg = out_4; a2 = out_7; MemWrite = out_7; a3 = out_8; ALUOp0 = out_8; Branch = out_8;
  //   ALUSrc = out_3; op0 = in_1[0]; op1 = in_1[1]; op2 = in_1[2]; op3 = in_1[3]; op4 = in_1[4]; op5 = in_1[5];
  //   jump = out_11; RegWrite = out_5
endmodule

module ALU (
  input  [31:0] in_1,
  input  [31:0] in_2,
  input  [3:0] in_3,
  output [31:0] out_4,
  output out_5
);

  wire [31:0] adder_1_out, and_1_out, or_1_out, subtractor_1_out;

  assign and_1_out = in_2 & in_1;  // AND_Gate and_1, 32 bits wide
  assign or_1_out = in_2 | in_1;  // OR_Gate or_1, 32 bits wide
  Adder #(.width(32)) adder_1 (.a(in_2), .b(in_1), .out(adder_1_out));  // open: cin, cout
  Subtractor #(.width(32)) subtractor_1 (.a(in_2), .b(in_1), .out(subtractor_1_out));  // open: bin, bout
  Multiplexer #(.select(4), .width(32)) multiplexer_1 (
    .in0(and_1_out), .in1(or_1_out), .in2(adder_1_out), .in6(subtractor_1_out), .out(out_4), .sel(in_3));  // open: in3, in4, in5, in7, in8, in9, in10, in11, in12, in13, in14, in15, en
  Comparator #(.width(32), .mode("unsigned")) comparator_1 (.a(out_4), .b({32{1'b0}}), .eq(out_5));  // open: gt, lt
endmodule

module Register_file (
  input  [31:0] in_1,
  input  regWrite,
  input  [4:0] read_register1,
  input  [4:0] write_register,
  input  [4:0] read_register_2,
  output [31:0] out_6,
  output [31:0] out_7
);

  wire clock_1_out, demultiplexer_1_out0, demultiplexer_1_out1, demultiplexer_1_out2, demultiplexer_1_out3,
       demultiplexer_1_out4, demultiplexer_1_out5, demultiplexer_1_out6, demultiplexer_1_out7,
       demultiplexer_1_out8, demultiplexer_1_out9, demultiplexer_1_out10, demultiplexer_1_out11,
       demultiplexer_1_out12, demultiplexer_1_out13, demultiplexer_1_out14, demultiplexer_1_out15,
       demultiplexer_1_out16, demultiplexer_1_out17, demultiplexer_1_out18, demultiplexer_1_out19,
       demultiplexer_1_out20, demultiplexer_1_out21, demultiplexer_1_out22, demultiplexer_1_out23,
       demultiplexer_1_out24, demultiplexer_1_out25, demultiplexer_1_out26, demultiplexer_1_out27,
       demultiplexer_1_out28, demultiplexer_1_out29, demultiplexer_1_out30, demultiplexer_1_out31;
  wire [31:0] _1, _2, _3, _4, _5, _6, _7, _8, _9, _10, _11, _12, _13, _14, _15, _16, _17, _18, _19, _20, _21,
       _22, _23, _24, _25, _26, _27, _28, _29, _30, _31, _32;

  Demultiplexer #(.select(5)) demultiplexer_1 (
    .out0(demultiplexer_1_out0), .out1(demultiplexer_1_out1), .out2(demultiplexer_1_out2),
    .out3(demultiplexer_1_out3), .out4(demultiplexer_1_out4), .out5(demultiplexer_1_out5),
    .out6(demultiplexer_1_out6), .out7(demultiplexer_1_out7), .out8(demultiplexer_1_out8),
    .out9(demultiplexer_1_out9), .out10(demultiplexer_1_out10), .out11(demultiplexer_1_out11),
    .out12(demultiplexer_1_out12), .out13(demultiplexer_1_out13), .out14(demultiplexer_1_out14),
    .out15(demultiplexer_1_out15), .out16(demultiplexer_1_out16), .out17(demultiplexer_1_out17),
    .out18(demultiplexer_1_out18), .out19(demultiplexer_1_out19), .out20(demultiplexer_1_out20),
    .out21(demultiplexer_1_out21), .out22(demultiplexer_1_out22), .out23(demultiplexer_1_out23),
    .out24(demultiplexer_1_out24), .out25(demultiplexer_1_out25), .out26(demultiplexer_1_out26),
    .out27(demultiplexer_1_out27), .out28(demultiplexer_1_out28), .out29(demultiplexer_1_out29),
    .out30(demultiplexer_1_out30), .out31(demultiplexer_1_out31), .in(regWrite), .sel(write_register));  // open: en
  Clock clock_1 (.out(clock_1_out));
  Register #(.width(32)) register_1 (.D(in_1), .en(demultiplexer_1_out0), .Q(_1), .clk(clock_1_out));  // open: clr
  Register #(.width(32)) register_2 (.D(in_1), .en(demultiplexer_1_out1), .Q(_2), .clk(clock_1_out));  // open: clr
  Register #(.width(32)) register_3 (.D(in_1), .en(demultiplexer_1_out2), .Q(_3), .clk(clock_1_out));  // open: clr
  Register #(.width(32)) register_4 (.D(in_1), .en(demultiplexer_1_out3), .Q(_4), .clk(clock_1_out));  // open: clr
  Register #(.width(32)) register_5 (.D(in_1), .en(demultiplexer_1_out4), .Q(_5), .clk(clock_1_out));  // open: clr
  Register #(.width(32)) register_6 (.D(in_1), .en(demultiplexer_1_out5), .Q(_6), .clk(clock_1_out));  // open: clr
  Register #(.width(32)) register_7 (.D(in_1), .en(demultiplexer_1_out6), .Q(_7), .clk(clock_1_out));  // open: clr
  Register #(.width(32)) register_8 (.D(in_1), .en(demultiplexer_1_out7), .Q(_8), .clk(clock_1_out));  // open: clr
  Register #(.width(32)) register_9 (.D(in_1), .en(demultiplexer_1_out8), .Q(_9), .clk(clock_1_out));  // open: clr
  Register #(.width(32)) register_10 (.D(in_1), .en(demultiplexer_1_out9), .Q(_10), .clk(clock_1_out));  // open: clr
  Register #(.width(32)) register_11 (.D(in_1), .en(demultiplexer_1_out10), .Q(_11), .clk(clock_1_out));  // open: clr
  Register #(.width(32)) register_12 (.D(in_1), .en(demultiplexer_1_out11), .Q(_12), .clk(clock_1_out));  // open: clr
  Register #(.width(32)) register_13 (.D(in_1), .en(demultiplexer_1_out12), .Q(_13), .clk(clock_1_out));  // open: clr
  Register #(.width(32)) register_14 (.D(in_1), .en(demultiplexer_1_out13), .Q(_14), .clk(clock_1_out));  // open: clr
  Register #(.width(32)) register_15 (.D(in_1), .en(demultiplexer_1_out14), .Q(_15), .clk(clock_1_out));  // open: clr
  Register #(.width(32)) register_16 (.D(in_1), .en(demultiplexer_1_out15), .Q(_16), .clk(clock_1_out));  // open: clr
  Register #(.width(32)) register_17 (.D(in_1), .en(demultiplexer_1_out16), .Q(_17), .clk(clock_1_out));  // open: clr
  Register #(.width(32)) register_18 (.D(in_1), .en(demultiplexer_1_out17), .Q(_18), .clk(clock_1_out));  // open: clr
  Register #(.width(32)) register_19 (.D(in_1), .en(demultiplexer_1_out18), .Q(_19), .clk(clock_1_out));  // open: clr
  Register #(.width(32)) register_20 (.D(in_1), .en(demultiplexer_1_out19), .Q(_20), .clk(clock_1_out));  // open: clr
  Register #(.width(32)) register_21 (.D(in_1), .en(demultiplexer_1_out20), .Q(_21), .clk(clock_1_out));  // open: clr
  Register #(.width(32)) register_22 (.D(in_1), .en(demultiplexer_1_out21), .Q(_22), .clk(clock_1_out));  // open: clr
  Register #(.width(32)) register_23 (.D(in_1), .en(demultiplexer_1_out22), .Q(_23), .clk(clock_1_out));  // open: clr
  Register #(.width(32)) register_24 (.D(in_1), .en(demultiplexer_1_out23), .Q(_24), .clk(clock_1_out));  // open: clr
  Register #(.width(32)) register_25 (.D(in_1), .en(demultiplexer_1_out24), .Q(_25), .clk(clock_1_out));  // open: clr
  Register #(.width(32)) register_26 (.D(in_1), .en(demultiplexer_1_out25), .Q(_26), .clk(clock_1_out));  // open: clr
  Register #(.width(32)) register_27 (.D(in_1), .en(demultiplexer_1_out26), .Q(_27), .clk(clock_1_out));  // open: clr
  Register #(.width(32)) register_28 (.D(in_1), .en(demultiplexer_1_out27), .Q(_28), .clk(clock_1_out));  // open: clr
  Register #(.width(32)) register_29 (.D(in_1), .en(demultiplexer_1_out28), .Q(_29), .clk(clock_1_out));  // open: clr
  Register #(.width(32)) register_30 (.D(in_1), .en(demultiplexer_1_out29), .Q(_30), .clk(clock_1_out));  // open: clr
  Register #(.width(32)) register_31 (.D(in_1), .en(demultiplexer_1_out30), .Q(_31), .clk(clock_1_out));  // open: clr
  Register #(.width(32)) register_32 (.D(in_1), .en(demultiplexer_1_out31), .Q(_32), .clk(clock_1_out));  // open: clr
  Multiplexer #(.select(5), .width(32)) multiplexer_1 (
    .in0(_1), .in1(_2), .in2(_3), .in3(_4), .in4(_5), .in5(_6), .in6(_7), .in7(_8), .in8(_9), .in9(_10),
    .in10(_11), .in11(_12), .in12(_13), .in13(_14), .in14(_15), .in15(_16), .in16(_17), .in17(_18),
    .in18(_19), .in19(_20), .in20(_21), .in21(_22), .in22(_23), .in23(_24), .in24(_25), .in25(_26),
    .in26(_27), .in27(_28), .in28(_29), .in29(_30), .in30(_31), .in31(_32), .out(out_6), .sel(read_register1));  // open: en
  Multiplexer #(.select(5), .width(32)) multiplexer_2 (
    .in0(_1), .in1(_2), .in2(_3), .in3(_4), .in4(_5), .in5(_6), .in6(_7), .in7(_8), .in8(_9), .in9(_10),
    .in10(_11), .in11(_12), .in12(_13), .in13(_14), .in14(_15), .in15(_16), .in16(_17), .in17(_18),
    .in18(_19), .in19(_20), .in20(_21), .in21(_22), .in22(_23), .in23(_24), .in24(_25), .in25(_26),
    .in26(_27), .in27(_28), .in28(_29), .in29(_30), .in30(_31), .in31(_32), .out(out_7), .sel(read_register_2));  // open: en

  // Notes on the sheet:
  //   write data
  //   read data 1
  //   read data 2
endmodule

module PC_Control (
  input  Zero,
  input  BNE,
  input  BEQ,
  input  Jump,
  output [1:0] PC
);

  wire and_1_out, and_2_out;

  or or_1 (PC[0], and_1_out, and_2_out);
  and and_1 (and_1_out, ~Zero, BNE);  // AND_Gate
  and and_2 (and_2_out, Zero, BEQ);

  assign PC[1] = Jump;
endmodule
